# Fritzing sketch LIDAR Node (saved by Fritzing 0.9.5d)

parts:
  Part2 = Arduino Mega 2560 (Rev3)
  Part3 = Arduino Ethernet Shield (Rev3)  # not connected
  JP1 = Header 12 [package=1x12_machine-pin-header_lock.004]
  JP2 = Header 12 [package=1x12_machine-pin-header_lock.004]

nets:
  N1: Part2.D17_PWM/RX2, JP2.6
  N2: Part2.D16_PWM/TX2, JP2.9
  N3: Part2.5V, JP2.5, JP2.11
  N4: Part2.GND, JP2.8
  N5: JP1.10, JP2.10
  N6: JP2.7, JP2.12
