# Fritzing sketch TOUCH Node (saved by Fritzing 0.9.5d)

parts:
  Part1 = Maker Uno (Arduino Uno Compatible)
  Part2 = MPR121 Breakout
  J2 = shrouded pin header, 10 pins [form="♂ (shrouded male)"]

nets:
  N1: Part1.D9_PWM, J2.pin7
  N2: Part1.D10_PWM/SS, J2.pin4
  N3: Part1.D11_PWM/MOSI, J2.pin3
  N4: Part1.D12/MISO, J2.pin9
  N5: Part1.D13/SCK, J2.pin8
  GND: Part1.GND, Part2.GND, J2.pin6
  N6: Part1.A4/SDA, Part2.SDA
  N7: Part1.A5/SCL, Part2.SCL
  N8: Part1.D2, Part2.~IRQ
  3V3: Part1.3V3, Part2.3.3V
  N9: Part1.5V, J2.pin5

custom parts:
  Maker Uno (Arduino Uno Compatible): Maker Uno, an Arduino UNO compatible board designed and developed specially for students to learn coding and microcontroller. We named it Maker UNO to encourage everyone to be a maker by getting started with this amazing board. Oh! BTW, it is PURPLE color.
